// Logisim project DDCA Project even parity.circ as structural Verilog: 1 circuit, main circuit main
module main (
  input  A,
  input  B,
  input  C,
  output Even_Parity
);

  wire xor_1_out;

  xor xor_1 (xor_1_out, A, B);
  xor xor_2 (Even_Parity, xor_1_out, C);
endmodule
